# Fritzing sketch DoorDetector (saved by Fritzing 0.9.5d)
breadboards: 1

parts:
  Composant1 = Arduino Uno (Rev3) - ICSP
  J1 = Piezo Speaker
  HC-SR04_Sensor_1 = HC-SR04 Ultrasonic Distance Sensor

nets:
  N1: Composant1.D2, J1.pin2
  N2: Composant1.D4, HC-SR04_Sensor_1.ECHO
  N3: Composant1.D5_PWM, HC-SR04_Sensor_1.TRIG
  5V: Composant1.5V, HC-SR04_Sensor_1.VCC
  GND: Composant1.GND, J1.pin1, HC-SR04_Sensor_1.GND
